# Fritzing sketch shéma electrique entier physique (saved by Fritzing 0.9.3b)
breadboards: 1

parts:
  M1 = DC Motor
  IC1 = L293D [package=THT]
  Composant1 = Arduino Uno (Rev3) - ICSP
  Composant3 = Real Time Clock Module - DS1307 RTC Breakout Board
  VCC1 = Battery block 9V
  S1 = Pushbutton [package="[THT]"]
  R1 = Resistor [tolerance=±5% resistance=220 package=THT]
  S2 = Pushbutton [package="[THT]"]
  R2 = Resistor [tolerance=±5% resistance=220 package=THT]

nets:
  N1: M1.pin_1, IC1.Out_4_(_Controlled_by_Enable_2_)
  N2: M1.pin_2, IC1.Out_3_(_Controlled_by_Enable_2_)
  GND: IC1.0V, Composant1.GND, Composant3.GND, VCC1.-, R1.Pin_1, R2.Pin_1
  N3: IC1.+Vmotor, IC1.+V, VCC1.+
  N4: IC1.Enable_2, Composant1.D3_PWM
  N5: IC1.In_3, Composant1.D4
  N6: IC1.In_4, Composant1.D2
  N7: Composant1.A4/SDA, Composant3.SCL
  N8: Composant1.A5/SCL, Composant3.SDA
  N9: Composant1.D5_PWM, S1.Pin_1, S1.Pin_2, R1.Pin_0
  5V: Composant1.D6_PWM, Composant1.5V, Composant3.5V, S1.Pin_3, S1.Pin_4, S2.Pin_3, S2.Pin_4
  N10: S2.Pin_1, S2.Pin_2, R2.Pin_0
